# Fritzing sketch 4g1-Breadboard_Switches_In_Parallel_With_Main_Switch (saved by Fritzing 0.9.3b)
breadboards: 1

parts:
  Micro_bit1 = Microbit
  S1 = Momentary Switch [package=ksa_sealed_tac_switch]
  S2 = Momentary Switch [package=ksa_sealed_tac_switch]

nets:
  N1: Micro_bit1.GND, S1.1, S2.1
  N2: Micro_bit1.5, S1.3
  N3: Micro_bit1.11, S2.3

notes:
  Pin 5
  0v or GND Pin
  BBC micro:bit
  Breadboard
  +
  -
  Pin 11
  Switch 1
  Switch 2

custom parts:
  Microbit: BBC Microbit Fritzing part
